# Fritzing sketch led-indicators (saved by Fritzing 0.9.4)
circuit board: 7cm x 2cm
breadboards: 1

parts:
  R1 = Resistor [tolerance=±5% resistance=220 package=THT]
  R2 = Resistor [tolerance=±5% resistance=220 package=THT]
  Green = LED - 5mm [color="Green (555nm)" package="5 mm [THT]"]
  Red = LED - 5mm [color="Red (633nm)" package="5 mm [THT]"]
  Single_LED = male pin header, 3 pins [form="♂ (male)"]

nets:
  N1: R1.Pin_0, Red.anode
  N2: R1.Pin_1, R2.Pin_1, Single_LED.pin1
  N3: R2.Pin_0, Green.anode
  N4: Green.cathode, Single_LED.pin3
  N5: Red.cathode, Single_LED.pin2
