# Fritzing sketch mainboard (saved by Fritzing 0.9.4)
circuit board: 10.2cm x 7cm
breadboards: 1

parts:
  Arduino_Nano = Arduino Nano (Rev3.0)
  Voltage_regulator = Voltage Regulator - 5V [package="TO220 [THT]"]
  Power = male pin header, 2 pins [form="♂ (male)"]
  ON/OFF = male pin header, 2 pins [form="♂ (male)"]
  SD_reader = male pin header, 6 pins [form="♂ (male)"]
  Single_LED = male pin header, 3 pins [form="♂ (male)"]
  Buttons = male pin header, 5 pins [form="♂ (male)"]
  Strip_LED = male pin header, 4 pins [form="♂ (male)"]
  R1 = Resistor [tolerance=±5% resistance=10k package=THT]
  R2 = Resistor [tolerance=±5% resistance=1k package=THT]
  R3 = Resistor [tolerance=±5% resistance=10k package=THT]
  R4 = Resistor [tolerance=±5% resistance=1k package=THT]
  R5 = Resistor [tolerance=±5% resistance=10k package=THT]
  R6 = Resistor [tolerance=±5% resistance=1k package=THT]
  Q1 = TIP120 Hi-Current Darlington Transistor
  Q2 = TIP120 Hi-Current Darlington Transistor
  Q3 = TIP120 Hi-Current Darlington Transistor
  Blue = male pin header, 4 pins [form="♂ (male)"]
  Green = male pin header, 4 pins [form="♂ (male)"]
  Red = male pin header, 4 pins [form="♂ (male)"]
  Intensity = male pin header, 4 pins [form="♂ (male)"]

nets:
  GND: Arduino_Nano.GND, Voltage_regulator.GND, Power.pin1, SD_reader.pin6, Single_LED.pin1, Buttons.pin1, R1.Pin_0, R3.Pin_0, R5.Pin_0, Q1.EMITTER, Q2.EMITTER, Q3.EMITTER, Blue.pin1, Green.pin1, Red.pin1, Intensity.pin1
  N1: Arduino_Nano.D2, Buttons.pin3
  N2: Arduino_Nano.D3, R6.Pin_1
  N3: Arduino_Nano.D4, Buttons.pin4
  N4: Arduino_Nano.D5, R4.Pin_1
  N5: Arduino_Nano.D6, R2.Pin_1
  N6: Arduino_Nano.D7, Buttons.pin5
  N7: Arduino_Nano.D8, SD_reader.pin1
  N8: Arduino_Nano.D9, Single_LED.pin2
  N9: Arduino_Nano.D10, Single_LED.pin3
  N10: Arduino_Nano.D11/MOSI, SD_reader.pin3
  N11: Arduino_Nano.D12/MISO, SD_reader.pin4
  N12: Arduino_Nano.VIN, Voltage_regulator.output_voltage
  N13: Arduino_Nano.5V, SD_reader.pin5, Buttons.pin2, Blue.pin2, Green.pin2, Red.pin2, Intensity.pin2
  N14: Arduino_Nano.A7, Blue.pin4
  N15: Arduino_Nano.A6, Blue.pin3
  N16: Arduino_Nano.A5, Green.pin4
  N17: Arduino_Nano.A4, Green.pin3
  N18: Arduino_Nano.A3, Red.pin4
  N19: Arduino_Nano.A2, Red.pin3
  N20: Arduino_Nano.A1, Intensity.pin4
  N21: Arduino_Nano.A0, Intensity.pin3
  N22: Arduino_Nano.D13/SCK, SD_reader.pin2
  N23: Voltage_regulator.input_voltage, ON/OFF.pin1, Strip_LED.pin4
  N24: Power.pin2, ON/OFF.pin2
  N25: Strip_LED.pin1, Q1.COLLECTOR
  N26: Strip_LED.pin2, Q2.COLLECTOR
  N27: Strip_LED.pin3, Q3.COLLECTOR
  N28: R1.Pin_1, R2.Pin_0, Q1.BASE
  N29: R3.Pin_1, R4.Pin_0, Q2.BASE
  N30: R5.Pin_1, R6.Pin_0, Q3.BASE
