# Fritzing sketch profiles-buttons (saved by Fritzing 0.9.4)
circuit board: 7cm x 2cm
breadboards: 1

parts:
  B1 = Pushbutton [package="[THT]"]
  B2 = Pushbutton [package="[THT]"]
  B3 = Pushbutton [package="[THT]"]
  R1 = Resistor [tolerance=±5% resistance=10k package=THT]
  R2 = Resistor [tolerance=±5% resistance=10k package=THT]
  R3 = Resistor [tolerance=±5% resistance=10k package=THT]
  Mainboard = male pin header, 5 pins [form="♂ (male)"]

nets:
  N1: B1.Pin_1, B1.Pin_2, R1.Pin_0, Mainboard.pin3
  N2: B1.Pin_3, B1.Pin_4, B2.Pin_3, B2.Pin_4, B3.Pin_3, B3.Pin_4, Mainboard.pin2
  N3: B2.Pin_1, B2.Pin_2, R2.Pin_0, Mainboard.pin4
  N4: B3.Pin_1, B3.Pin_2, R3.Pin_0, Mainboard.pin5
  N5: R1.Pin_1, R2.Pin_1, R3.Pin_1, Mainboard.pin1
